# Fritzing sketch Bike_Alarm (saved by Fritzing 0.9.6b)
circuit board: 5.43006cm x 7.09896cm
breadboards: 1

parts:
  R5 = Resistor [tolerance=±5% power=0.25 resistance=100 package=THT]
  LED2 = LED - 5mm [color="Red (633nm)" current=0.030 package="5 mm [THT]"]
  LED4 = LED - 5mm [color="Red (633nm)" current=0.030 package="5 mm [THT]"]
  IR1 = TSOP312.., 314.. [package=THT]
  HC-SR04_Sensor_1 = HC-SR04 Ultrasonic Distance Sensor
  R2 = Resistor [tolerance=±5% power=0.25 resistance=220 package=THT]
  R3 = Resistor [tolerance=±5% power=0.25 resistance=220 package=THT]
  R4 = Resistor [tolerance=±5% power=0.25 resistance=220 package=THT]
  ATMega328 = atmega328 [package=dip]
  SPKR1 = Loudspeaker
  LED3 = LED - 5mm [color="Red (633nm)" current=0.030 package="5 mm [THT]"]
  VCC1 = Battery block 9V

nets (from the pcb view):
  N1: R5.Pin_0, IR1.GND, R2.Pin_0, R3.Pin_0, R4.Pin_0, ATMega328.GND#21, VCC1.-
  N2: R5.Pin_1, SPKR1.pin1
  N3: LED2.cathode, R4.Pin_1
  N4: LED2.anode, LED4.anode, ATMega328.A1, LED3.anode
  N5: LED4.cathode, R2.Pin_1
  VCC: IR1.Vs, HC-SR04_Sensor_1.VCC, ATMega328.VCC, VCC1.+
  N6: IR1.Data, ATMega328.A0
  N7: HC-SR04_Sensor_1.ECHO, ATMega328.D7
  N8: HC-SR04_Sensor_1.GND, ATMega328.GND#7
  N9: R3.Pin_1, LED3.cathode
  N10: ATMega328.A2, SPKR1.pin2

// code stored in the sketch: Arduino_Alarm.ino

const byte IR_SENSOR=A0;
const byte LIGHTS_PIN=A1;
const byte ALARM=A2;
const byte ACTIVATED_PIN=A3;
const byte DISTANCE_SENSORS[] = {7,7};

const float CMS_CONVERTER = 0.01723;
const byte TRIGGER_DISTANCE = 100;
unsigned long currentMillis;

long DISTANCE = 500;
bool ACTIVATED = false;
bool IR_PRESSED = false;
//Alarm.
unsigned long previousMillis = 0;
const long interval = 200;
int ALARM_STATE = LOW;

void setup() {
  Serial.begin(9600);
  pinMode(IR_SENSOR,INPUT);
  pinMode(LIGHTS_PIN,OUTPUT);
  pinMode(ACTIVATED_PIN,OUTPUT);
  pinMode(ALARM,OUTPUT);
}

void loop(){
  currentMillis = millis();
  readRemoteSignal();
  readDistanceSensor();
  //Serial.print(DISTANCE); Serial.println("cm");
  if(ACTIVATED){
    if(DISTANCE<=TRIGGER_DISTANCE){ soundAlarm(); }
    else{ stopAlarm(); }
  }
}
void readRemoteSignal(){
  if(digitalRead(IR_SENSOR)==LOW && !IR_PRESSED) {
	IR_PRESSED=true;
    ACTIVATED=!ACTIVATED;
    digitalWrite(ACTIVATED_PIN,ACTIVATED?HIGH:LOW);
    delay(500);
    Serial.print("ACTIVATED:"); Serial.println(ACTIVATED?"ON":"OFF");
  }else{ IR_PRESSED=false; }
}

void readDistanceSensor() {
  pinMode(DISTANCE_SENSORS[0], OUTPUT);  // Clear the trigger
  digitalWrite(DISTANCE_SENSORS[0], LOW);
  delayMicroseconds(2);
  // Sets the trigger pin to HIGH state for 10 microseconds
  digitalWrite(DISTANCE_SENSORS[0], HIGH);
  delayMicroseconds(10);
  digitalWrite(DISTANCE_SENSORS[0], LOW);
  pinMode(DISTANCE_SENSORS[1], INPUT);
  // Reads the echo pin, and returns the sound wave travel time in microseconds
  //return 0.01723 * pulseIn(DISTANCE_SENSORS[1], HIGH);
  DISTANCE = CMS_CONVERTER * pulseIn(DISTANCE_SENSORS[1], HIGH);
}

void soundAlarm(){
  if (currentMillis - previousMillis >= interval) {
    previousMillis = currentMillis;
    ALARM_STATE = ALARM_STATE==LOW? HIGH:LOW;
  	digitalWrite(LIGHTS_PIN,ALARM_STATE); 
    tone(ALARM, 1300, 100);
  }
  
}

void stopAlarm(){
  ALARM_STATE=LOW;
  digitalWrite(ALARM,LOW);
  digitalWrite(LIGHTS_PIN,LOW);
}
